// Logisim project jrmips.circ as structural Verilog: 21 circuits, main circuit main
module main (
);

  wire alu_main_circuit_1_load, alu_main_circuit_1_store, Clock_out, decoder_main_circuit_1_cpu,
       decoder_main_circuit_1_system_opcode, decoder_main_circuit_1_word_opcode, or_1_out;
  wire [1:0] decoder_main_circuit_1_type;
  wire [2:0] decoder_main_circuit_1_alu_opcode, decoder_main_circuit_1_branch_opcode;
  wire [3:0] alu_main_circuit_1_display_output_2, alu_main_circuit_1_display_output_3,
       decoder_main_circuit_1_shamt_output;
  wire [7:0] adder_1_out, alu_main_circuit_1_address_output, alu_main_circuit_1_display_output,
       alu_main_circuit_1_pc_output, decoder_main_circuit_1_branch_con__output,
       decoder_main_circuit_1_immediate_output, decoder_main_circuit_1_pc_output, register_1_q;
  wire [15:0] alu_main_circuit_1_alu_output, alu_main_circuit_1_branch_ouput, alu_main_circuit_1_word_output,
       decoder_main_circuit_1_rs_output, decoder_main_circuit_1_rt_output, multiplexer_1_out, ram_1_data,
       rom_1_data;

  Register_part register_1 (
    .D(decoder_main_circuit_1_pc_output), .en(decoder_main_circuit_1_cpu), .Q(register_1_q), .clk(Clock_out));  // open: clr
  LED led_1 (.in(decoder_main_circuit_1_cpu));
  Clock Clock (.out(Clock_out));
  Adder adder_1 (.a(8'h1), .b(register_1_q), .out(adder_1_out));  // open: cin, cout
  ROM #(.dataWidth(16)) rom_1 (.addr(register_1_q), .data(rom_1_data), .sel(1'b1));
  Decoder_Main_Circuit decoder_main_circuit_1 (
    .PC_Output(decoder_main_circuit_1_pc_output), .PC_Input(adder_1_out), .Instruction(rom_1_data),
    .Write_Register(multiplexer_1_out), .Type(decoder_main_circuit_1_type),
    .ALU_Opcode(decoder_main_circuit_1_alu_opcode), .Branch_Opcode(decoder_main_circuit_1_branch_opcode),
    .Word_Opcode(decoder_main_circuit_1_word_opcode), .System_Opcode(decoder_main_circuit_1_system_opcode),
    .Clock(Clock_out), .CPU(decoder_main_circuit_1_cpu), .Branch_Con_Input(alu_main_circuit_1_pc_output),
    .Branch_Con__Output(decoder_main_circuit_1_branch_con__output),
    .rs_Output(decoder_main_circuit_1_rs_output), .rt_Output(decoder_main_circuit_1_rt_output),
    .Immediate_Output(decoder_main_circuit_1_immediate_output),
    .shamt_Output(decoder_main_circuit_1_shamt_output));
  ALU_Main_Circuit alu_main_circuit_1 (
    .PC_Input(decoder_main_circuit_1_branch_con__output), .rs_Input(decoder_main_circuit_1_rs_output),
    .rt_Input(decoder_main_circuit_1_rt_output), .Immediate(decoder_main_circuit_1_immediate_output),
    .shamt_Input(decoder_main_circuit_1_shamt_output), .Branch_Opcode(decoder_main_circuit_1_branch_opcode),
    .System_Opcode(decoder_main_circuit_1_system_opcode), .ALU_Opcode(decoder_main_circuit_1_alu_opcode),
    .Type(decoder_main_circuit_1_type), .Word_Opcode(decoder_main_circuit_1_word_opcode), .Clock(Clock_out),
    .Display_Output({alu_main_circuit_1_display_output_3, alu_main_circuit_1_display_output_2, alu_main_circuit_1_display_output}),
    .Branch_Ouput(alu_main_circuit_1_branch_ouput), .PC_Output(alu_main_circuit_1_pc_output),
    .ALU_Output(alu_main_circuit_1_alu_output), .Word_Output(alu_main_circuit_1_word_output),
    .Address_Output(alu_main_circuit_1_address_output), .Store(alu_main_circuit_1_store),
    .Load(alu_main_circuit_1_load));
  Hex_Digit_Display hex_digit_display_1 (.value(alu_main_circuit_1_display_output_3), .dp(1'b0));
  or or_1 (or_1_out, alu_main_circuit_1_store, alu_main_circuit_1_load);
  Hex_Digit_Display hex_digit_display_2 (.value(alu_main_circuit_1_display_output_2), .dp(1'b0));
  Hex_Digit_Display hex_digit_display_3 (.value(alu_main_circuit_1_display_output[7:4]), .dp(1'b0));
  Hex_Digit_Display hex_digit_display_4 (.value(alu_main_circuit_1_display_output[3:0]), .dp(1'b0));
  RAM #(.dataWidth(16), .bus("separate")) ram_1 (
    .addr(alu_main_circuit_1_address_output), .din(alu_main_circuit_1_word_output), .data(ram_1_data),
    .str(alu_main_circuit_1_store), .sel(or_1_out), .clk(Clock_out), .ld(alu_main_circuit_1_load));  // open: clr
  Multiplexer #(.select(2), .width(16), .enable("false")) multiplexer_1 (
    .in0(alu_main_circuit_1_alu_output), .in1(alu_main_circuit_1_branch_ouput), .in2(ram_1_data),
    .out(multiplexer_1_out), .sel(decoder_main_circuit_1_type));  // open: in3

  // Notes on the sheet:
  //   Joey Reidell
  //   Jr.Mips
  //   JMR240@pitt.edu
  //   contents of rom_1 (hex, n*v repeats v):
  //   1fc1 2fff 1901 29ff 800 1001 2013 bc18 1901 2955 800 f000 2ffe 7dc1 0 9024 21fe bc18 7dc0 2e02 ac00
endmodule

module ALU (
  input  [15:0] rs_Input,
  input  [15:0] rt_Input,
  input  [2:0] Opcode,
  input  [3:0] shamt,
  output [15:0] rs_Output
);

  wire [15:0] adder_1_out, and_1_out, nor_1_out, shifter_1_out, shifter_2_out, subtractor_1_out;

  Adder #(.width(16)) adder_1 (.a(rs_Input), .b(rt_Input), .out(adder_1_out));  // open: cin, cout
  assign nor_1_out = ~(rs_Input | rt_Input);  // NOR_Gate nor_1, 16 bits wide
  Subtractor #(.width(16)) subtractor_1 (.a(rs_Input), .b(rt_Input), .out(subtractor_1_out));  // open: bin, bout
  assign and_1_out = rs_Input & rt_Input;  // AND_Gate and_1, 16 bits wide
  Shifter #(.width(16)) shifter_1 (.in(rs_Input), .\dist (shamt), .out(shifter_1_out));
  Shifter #(.width(16), .shift("lr")) shifter_2 (.in(rs_Input), .\dist (shamt), .out(shifter_2_out));
  Multiplexer #(.select(3), .width(16), .enable("false")) multiplexer_1 (
    .in0(adder_1_out), .in1(subtractor_1_out), .in2(and_1_out), .in3(nor_1_out), .in4(shifter_1_out),
    .in5(shifter_2_out), .out(rs_Output), .sel(Opcode));  // open: in6, in7

  // Notes on the sheet:
  //   ALU Subcircuit
endmodule

module Fetch (
  input  [15:0] Instruction_Input,
  output [1:0] Type,
  output Format,
  output [2:0] rs_Read,
  output [2:0] rt_Read,
  output [7:0] Immediate
);

  wire and_1_out, and_2_out, and_3_out, and_4_out, and_5_out, and_6_out, not_1_out, not_2_out, not_3_out,
       not_4_out, not_5_out, not_6_out, not_7_out, not_8_out, not_9_out, not_10_out, not_11_out;

  not not_1 (not_1_out, Instruction_Input[15]);
  not not_2 (not_2_out, Instruction_Input[14]);
  not not_3 (not_3_out, Instruction_Input[13]);
  not not_4 (not_4_out, Instruction_Input[12]);
  not not_5 (not_5_out, Instruction_Input[14]);
  not not_6 (not_6_out, Instruction_Input[13]);
  not not_7 (not_7_out, Instruction_Input[12]);
  not not_8 (not_8_out, Instruction_Input[15]);
  not not_9 (not_9_out, Instruction_Input[12]);
  not not_10 (not_10_out, Instruction_Input[13]);
  not not_11 (not_11_out, Instruction_Input[14]);
  and and_1 (and_1_out, not_1_out, not_2_out, not_3_out, not_4_out);
  and and_2 (and_2_out, Instruction_Input[14], Instruction_Input[13]);
  and and_3 (and_3_out, not_5_out, not_6_out, not_7_out);
  and and_4 (and_4_out, not_8_out, Instruction_Input[13], not_9_out);
  and and_5 (and_5_out, Instruction_Input[15], not_10_out);
  and and_6 (and_6_out, Instruction_Input[15], not_11_out, Instruction_Input[12]);
  or or_1 (Type[1], and_1_out, and_2_out);
  or or_2 (Type[0], and_3_out, Instruction_Input[15]);
  or or_3 (Format, and_4_out, and_5_out, and_6_out);

  assign Immediate = Instruction_Input[8:1];
  assign rs_Read = Instruction_Input[11:9];
  assign rt_Read = Instruction_Input[8:6];

  // Notes on the sheet:
  //   Fetch Subcircuit
endmodule

module ALU_Control (
  input  [15:0] Instruction_Input,
  output ALU_2,
  output ALU_1,
  output ALU_0,
  output Sub_Opcode
);

  wire and_2_out, and_3_out, not_1_out;

  not not_1 (not_1_out, Instruction_Input[13]);
  and and_1 (ALU_1, Instruction_Input[13], Instruction_Input[12]);
  and and_2 (and_2_out, not_1_out, Instruction_Input[0]);
  and and_3 (and_3_out, Instruction_Input[12], Instruction_Input[0]);
  or or_1 (ALU_0, and_2_out, and_3_out);

  assign ALU_2 = Instruction_Input[14];
  assign Sub_Opcode = Instruction_Input[0];

  // Notes on the sheet:
  //   ALU Control Subcircuit
endmodule

module Decoder (
  input  [15:0] Instruction_Input,
  input  [1:0] Control_Type,
  output [2:0] ALU_Select,
  output Sub_Opcode,
  output [2:0] Branch_Select,
  output Word_Select,
  output System_Select,
  output CPU
);

  wire [15:0] demultiplexer_1_out0, demultiplexer_1_out1, demultiplexer_1_out2, demultiplexer_1_out3;

  Demultiplexer #(.select(2), .width(16), .disabled(0), .enable("false")) demultiplexer_1 (
    .out0(demultiplexer_1_out0), .out1(demultiplexer_1_out1), .out2(demultiplexer_1_out2),
    .out3(demultiplexer_1_out3), .in(Instruction_Input), .sel(Control_Type));
  ALU_Control ALU_Con (
    .Instruction_Input(demultiplexer_1_out0), .ALU_2(ALU_Select[2]), .ALU_1(ALU_Select[1]),
    .ALU_0(ALU_Select[0]), .Sub_Opcode(Sub_Opcode));
  Branch_Control Branch_Con (
    .Instruction_Input(demultiplexer_1_out1), .Branch_2(Branch_Select[2]), .Branch_1(Branch_Select[1]),
    .Branch_0(Branch_Select[0]));
  Word_Control Word_Con (.Instruction_Input(demultiplexer_1_out2), .Word(Word_Select));
  System_Control Sys__Con (.Instruction_Input(demultiplexer_1_out3), .System0(System_Select));
  not not_1 (CPU, System_Select);

  // Notes on the sheet:
  //   Decoder Subcircuit
endmodule

module Register (
  input  [2:0] rs_Control,
  input  [15:0] Register_Writer,
  input  Write,
  input  [2:0] rt_Control,
  input  Clock,
  output [15:0] rs_Ouput,
  output [15:0] rt_Output
);

  wire decoder_1_out0, decoder_1_out1, decoder_1_out2, decoder_1_out3, decoder_1_out4, decoder_1_out5,
       decoder_1_out6, decoder_1_out7;
  wire [15:0] demultiplexer_1_out0, demultiplexer_1_out1, demultiplexer_1_out2, demultiplexer_1_out3,
       demultiplexer_1_out4, demultiplexer_1_out5, demultiplexer_1_out6, demultiplexer_1_out7, r0_q, r1_q,
       r2_q, r3_q, r4_q, r5_q, r6_q, r7_q;

  Demultiplexer #(.select(3), .width(16), .disabled(0)) demultiplexer_1 (
    .out0(demultiplexer_1_out0), .out1(demultiplexer_1_out1), .out2(demultiplexer_1_out2),
    .out3(demultiplexer_1_out3), .out4(demultiplexer_1_out4), .out5(demultiplexer_1_out5),
    .out6(demultiplexer_1_out6), .out7(demultiplexer_1_out7), .in(Register_Writer), .sel(rs_Control),
    .en(Write));
  Decoder_part #(.select(3), .disabled(0)) decoder_1 (
    .out0(decoder_1_out0), .out1(decoder_1_out1), .out2(decoder_1_out2), .out3(decoder_1_out3),
    .out4(decoder_1_out4), .out5(decoder_1_out5), .out6(decoder_1_out6), .out7(decoder_1_out7),
    .sel(rs_Control), .en(Write));
  Register_part #(.width(16)) r0 (.D(demultiplexer_1_out0), .en(decoder_1_out0), .Q(r0_q), .clk(Clock));  // open: clr
  Register_part #(.width(16)) r1 (.D(demultiplexer_1_out1), .en(decoder_1_out1), .Q(r1_q), .clk(Clock));  // open: clr
  Register_part #(.width(16)) r2 (.D(demultiplexer_1_out2), .en(decoder_1_out2), .Q(r2_q), .clk(Clock));  // open: clr
  Register_part #(.width(16)) r3 (.D(demultiplexer_1_out3), .en(decoder_1_out3), .Q(r3_q), .clk(Clock));  // open: clr
  Register_part #(.width(16)) r4 (.D(demultiplexer_1_out4), .en(decoder_1_out4), .Q(r4_q), .clk(Clock));  // open: clr
  Register_part #(.width(16)) r5 (.D(demultiplexer_1_out5), .en(decoder_1_out5), .Q(r5_q), .clk(Clock));  // open: clr
  Register_part #(.width(16)) r6 (.D(demultiplexer_1_out6), .en(decoder_1_out6), .Q(r6_q), .clk(Clock));  // open: clr
  Register_part #(.width(16)) r7 (.D(demultiplexer_1_out7), .en(decoder_1_out7), .Q(r7_q), .clk(Clock));  // open: clr
  Multiplexer #(.select(3), .width(16), .enable("false")) multiplexer_1 (
    .in0(r0_q), .in1(r1_q), .in2(r2_q), .in3(r3_q), .in4(r4_q), .in5(r5_q), .in6(r6_q), .in7(r7_q),
    .out(rt_Output), .sel(rt_Control));
  Multiplexer #(.select(3), .width(16), .enable("false")) multiplexer_2 (
    .in0(r0_q), .in1(r1_q), .in2(r2_q), .in3(r3_q), .in4(r4_q), .in5(r5_q), .in6(r6_q), .in7(r7_q),
    .out(rs_Ouput), .sel(rs_Control));

  // Notes on the sheet:
  //   Registers Subcircuit
endmodule

// Sign
module Sign_Extender (
  input  [7:0] Immediate_Input,
  input  Sub_Opcode,
  output [15:0] Immedite_Output
);

  wire [15:0] bit_extender_1_out, bit_extender_2_out;

  assign bit_extender_1_out = {{8{Immediate_Input[7]}}, Immediate_Input};  // Bit_Extender bit_extender_1
  assign bit_extender_2_out = {{8{1'b0}}, Immediate_Input};  // Bit_Extender bit_extender_2
  Multiplexer #(.width(16), .enable("false")) multiplexer_1 (
    .in0(bit_extender_1_out), .in1(bit_extender_2_out), .out(Immedite_Output), .sel(Sub_Opcode));

  // Notes on the sheet:
  //   Sign Extender Subcircuit
endmodule

module Display (
  input  [15:0] rs_Input,
  input  [1:0] Type_Input,
  input  System_Select,
  input  Clock,
  output [15:0] Display
);

  wire and_1_out, Display_Con_output, not_1_out;

  Display_Control Display_Con (
    .Type1(Type_Input[1]), .Type0(Type_Input[0]), .System0(System_Select), .Output(Display_Con_output));
  not not_1 (not_1_out, Clock);
  Register_part #(.width(16)) register_1 (.D(rs_Input), .en(1'b1), .Q(Display), .clk(and_1_out));  // open: clr
  and and_1 (and_1_out, not_1_out, Display_Con_output);

  // Notes on the sheet:
  //   Display Subcircuit
endmodule

module Branch_Control (
  input  [15:0] Instruction_Input,
  output Branch_2,
  output Branch_1,
  output Branch_0
);


  assign Branch_0 = Instruction_Input[12];
  assign Branch_1 = Instruction_Input[13];
  assign Branch_2 = Instruction_Input[14];

  // Notes on the sheet:
  //   Branch Control Subcircuit
endmodule

module Branch (
  input  [2:0] Branch_Opcode,
  input  [7:0] PC_Input,
  input  [15:0] rs,
  input  [7:0] Immediate,
  output [15:0] Output,
  output [7:0] PC_Output
);

  wire Branch_Con_2_dmx, Branch_Con_2_dmx_combo, Branch_Con_2_jal_buffer, bx_circuit_1_not_equal,
       bz_circuit_1_equal, multiplexer_1_out;
  wire [7:0] bit_extender_1_out, controlled_buffer_1_out, multiplexer_2_out;
  wire [15:0] demultiplexer_1_out0, demultiplexer_1_out1;

  _2nd_Branch_Control Branch_Con_2 (
    .Branch_Opcode2(Branch_Opcode[2]), .Branch_Opcode1(Branch_Opcode[1]), .Branch_Opcode0(Branch_Opcode[0]),
    .DMX_Combo(Branch_Con_2_dmx_combo), .DMX(Branch_Con_2_dmx), .jal_Buffer(Branch_Con_2_jal_buffer));
  Demultiplexer #(.width(16), .enable("false")) demultiplexer_1 (
    .out0(demultiplexer_1_out0), .out1(demultiplexer_1_out1), .in(rs), .sel(Branch_Con_2_dmx_combo));
  Bit_Extender #(.in_width(16), .out_width(8)) bit_extender_1 (.in(demultiplexer_1_out0), .out(bit_extender_1_out));
  BX_Circuit bx_circuit_1 (.rs(demultiplexer_1_out1), .Not_Equal(bx_circuit_1_not_equal));
  Multiplexer #(.disabled(0), .enable("false")) multiplexer_1 (
    .in0(bx_circuit_1_not_equal), .in1(bz_circuit_1_equal), .out(multiplexer_1_out), .sel(Branch_Con_2_dmx));
  BZ_Circuit bz_circuit_1 (.rs(demultiplexer_1_out1), .Equal(bz_circuit_1_equal));
  assign controlled_buffer_1_out = Branch_Con_2_jal_buffer ? PC_Input : 8'bz;  // Controlled_Buffer controlled_buffer_1
  Multiplexer #(.width(8), .disabled(0), .enable("false")) multiplexer_2 (
    .in0(PC_Input), .in1(Immediate), .out(multiplexer_2_out), .sel(multiplexer_1_out));
  assign Output = {{8{1'b0}}, controlled_buffer_1_out};  // Bit_Extender bit_extender_2
  Multiplexer #(.select(3), .width(8), .enable("false")) multiplexer_3 (
    .in0(multiplexer_2_out), .in1(multiplexer_2_out), .in2(bit_extender_1_out), .in3(Immediate),
    .in4(Immediate), .out(PC_Output), .sel(Branch_Opcode));  // open: in5, in6, in7

  // Notes on the sheet:
  //   Branch Subcircuit
endmodule

module Word (
  input  [15:0] rs_Data,
  input  Word_Opcode,
  input  [1:0] Type,
  input  [15:0] rt_data,
  output [15:0] Data_Output,
  output Store,
  output Load,
  output [7:0] Address_Output
);

  wire and_1_out, not_1_out, not_2_out;

  not not_1 (not_1_out, Type[0]);
  and and_1 (and_1_out, Type[1], not_1_out);
  Bit_Extender #(.in_width(16), .out_width(8)) bit_extender_1 (.in(rt_data), .out(Address_Output));
  and and_2 (Store, Word_Opcode, and_1_out);
  and and_3 (Load, and_1_out, not_2_out);
  not not_2 (not_2_out, Word_Opcode);
  assign Data_Output = Store ? rs_Data : 16'bz;  // Controlled_Buffer controlled_buffer_1

  // Notes on the sheet:
  //   Word Subcircuit
endmodule

module Word_Control (
  input  [15:0] Instruction_Input,
  output Word
);


  assign Word = Instruction_Input[0];

  // Notes on the sheet:
  //   Word Control Subcircuit
endmodule

module Display_Control (
  input  Type1,
  input  Type0,
  input  System0,
  output Output
);

  wire not_1_out;

  not not_1 (not_1_out, System0);
  and and_1 (Output, Type1, Type0, not_1_out);

  // Notes on the sheet:
  //   Display Control Subcircuit
endmodule

module System_Control (
  input  [15:0] Instruction_Input,
  output System0
);


  assign System0 = Instruction_Input[15];

  // Notes on the sheet:
  //   System Control Subcircuit
endmodule

module _2nd_Branch_Control (
  input  Branch_Opcode2,
  input  Branch_Opcode1,
  input  Branch_Opcode0,
  output DMX_Combo,
  output DMX,
  output jal_Buffer
);

  not not_1 (DMX_Combo, Branch_Opcode0);
  and and_1 (jal_Buffer, Branch_Opcode0, Branch_Opcode1);

  assign DMX = Branch_Opcode1;

  // Notes on the sheet:
  //   2nd Branch Control Subcircuit
endmodule

module Bypass (
  input  [7:0] PC_Branch_1,
  input  [1:0] Type,
  input  [7:0] PC_Intput,
  output [7:0] PC_Ouput,
  output [7:0] PC_Branch0
);

  wire Bypass_Con_bypass;
  wire [7:0] demultiplexer_1_out0;

  Bypass_Control Bypass_Con (.Type_Input(Type), .Bypass(Bypass_Con_bypass));
  Multiplexer #(.width(8), .enable("false")) multiplexer_1 (
    .in0(demultiplexer_1_out0), .in1(PC_Branch_1), .out(PC_Ouput), .sel(Bypass_Con_bypass));
  Demultiplexer #(.width(8), .enable("false")) demultiplexer_1 (
    .out0(demultiplexer_1_out0), .out1(PC_Branch0), .in(PC_Intput), .sel(Bypass_Con_bypass));

  // Notes on the sheet:
  //   Bypass Subcircuit
endmodule

module Bypass_Control (
  input  [1:0] Type_Input,
  output Bypass
);

  wire not_1_out;

  not not_1 (not_1_out, Type_Input[1]);
  and and_1 (Bypass, not_1_out, Type_Input[0]);

  // Notes on the sheet:
  //   Bypass Control Subcircuit
endmodule

// BX
module BX_Circuit (
  input  [15:0] rs,
  output Not_Equal
);

  Comparator #(.width(16), .mode("unsigned")) comparator_1 (.a(rs), .b({16{1'b0}}), .gt(Not_Equal));  // open: eq, lt

  // Notes on the sheet:
  //   BX Circuit Subcircuit
endmodule

// BZ
module BZ_Circuit (
  input  [15:0] rs,
  output Equal
);

  Comparator #(.width(16), .mode("unsigned")) comparator_1 (.a(rs), .b({16{1'b0}}), .eq(Equal));  // open: gt, lt

  // Notes on the sheet:
  //   BZ Circuit Subcircuit
endmodule

// ALU Main
module ALU_Main_Circuit (
  input  [2:0] Branch_Opcode,
  input  System_Opcode,
  input  [7:0] PC_Input,
  input  [15:0] rs_Input,
  input  [15:0] rt_Input,
  input  [7:0] Immediate,
  input  [3:0] shamt_Input,
  input  [2:0] ALU_Opcode,
  input  [1:0] Type,
  input  Word_Opcode,
  input  Clock,
  output [15:0] Display_Output,
  output [15:0] Branch_Ouput,
  output [7:0] PC_Output,
  output [15:0] ALU_Output,
  output [15:0] Word_Output,
  output [7:0] Address_Output,
  output Store,
  output Load
);

  Display Display (
    .rs_Input(rs_Input), .Type_Input(Type), .System_Select(System_Opcode), .Clock(Clock),
    .Display(Display_Output));
  Branch Branch (
    .PC_Input(PC_Input), .rs(rs_Input), .Immediate(Immediate), .Branch_Opcode(Branch_Opcode),
    .Output(Branch_Ouput), .PC_Output(PC_Output));
  ALU alu_1 (
    .rs_Input(rs_Input), .rt_Input(rt_Input), .shamt(shamt_Input), .Opcode(ALU_Opcode), .rs_Output(ALU_Output));
  Word word_1 (
    .rs_Data(rs_Input), .rt_data(rt_Input), .Type(Type), .Word_Opcode(Word_Opcode),
    .Data_Output(Word_Output), .Store(Store), .Load(Load), .Address_Output(Address_Output));

  // Notes on the sheet:
  //   ALU Main Circuit Subcircuit
endmodule

// Decoder Main
module Decoder_Main_Circuit (
  input  [7:0] Branch_Con_Input,
  input  [7:0] PC_Input,
  input  [15:0] Instruction,
  input  [15:0] Write_Register,
  input  Clock,
  output [2:0] Branch_Opcode,
  output [1:0] Type,
  output [2:0] ALU_Opcode,
  output Word_Opcode,
  output System_Opcode,
  output [7:0] PC_Output,
  output [7:0] Branch_Con__Output,
  output [15:0] rs_Output,
  output [15:0] rt_Output,
  output [7:0] Immediate_Output,
  output CPU,
  output [3:0] shamt_Output
);

  wire decoder_1_sub_opcode, fetch_1_format;
  wire [2:0] fetch_1_rs_read, fetch_1_rt_read;
  wire [15:0] register_1_rt_output, sign_extender_1_immedite_output;

  Bypass Bypass (
    .PC_Ouput(PC_Output), .Type(Type), .PC_Intput(PC_Input), .PC_Branch_1(Branch_Con_Input),
    .PC_Branch0(Branch_Con__Output));
  Fetch fetch_1 (
    .Instruction_Input(Instruction), .Type(Type), .Format(fetch_1_format), .rs_Read(fetch_1_rs_read),
    .rt_Read(fetch_1_rt_read), .Immediate(Immediate_Output));
  Register register_1 (
    .rs_Control(fetch_1_rs_read), .Register_Writer(Write_Register), .Write(1'b1),
    .rt_Control(fetch_1_rt_read), .Clock(Clock), .rs_Ouput(rs_Output), .rt_Output(register_1_rt_output));
  Sign_Extender sign_extender_1 (
    .Immediate_Input(Immediate_Output), .Sub_Opcode(decoder_1_sub_opcode),
    .Immedite_Output(sign_extender_1_immedite_output));
  Decoder decoder_1 (
    .Instruction_Input(Instruction), .Control_Type(Type), .CPU(CPU), .ALU_Select(ALU_Opcode),
    .Sub_Opcode(decoder_1_sub_opcode), .Branch_Select(Branch_Opcode), .Word_Select(Word_Opcode),
    .System_Select(System_Opcode));
  Multiplexer #(.width(16), .enable("false")) multiplexer_1 (
    .in0(register_1_rt_output), .in1(sign_extender_1_immedite_output), .out(rt_Output), .sel(fetch_1_format));

  assign shamt_Output = Immediate_Output[3:0];

  // Notes on the sheet:
  //   Decoder Main Circuit Subcircuit
endmodule
